// Logisim project main.circ as structural Verilog: 7 circuits, main circuit main
module main (
  input  in_1,
  input  in_2,
  input  a,
  input  b,
  input  c,
  input  d,
  input  e,
  input  f,
  input  g,
  input  h,
  input  i,
  input  j,
  input  k,
  input  l,
  input  m,
  input  n,
  input  o,
  input  p,
  input  q,
  input  r,
  input  s,
  input  t,
  input  u,
  input  v,
  input  w,
  input  x,
  input  y,
  input  z,
  output a_2,
  output b_2,
  output c_2,
  output d_2,
  output e_2,
  output f_2,
  output g_2,
  output h_2,
  output i_2,
  output j_2,
  output k_2,
  output l_2,
  output m_2,
  output n_2,
  output o_2,
  output p_2,
  output q_2,
  output r_2,
  output s_2,
  output t_2,
  output u_2,
  output v_2,
  output w_2,
  output x_2,
  output y_2,
  output z_2
);

  wire and_1_out, and_2_out, and_3_out, and_4_out, and_5_out, and_6_out, and_7_out, and_8_out, and_9_out,
       and_10_out, and_11_out, and_12_out, and_13_out, and_14_out, and_15_out, and_16_out, and_17_out,
       and_18_out, and_19_out, and_20_out, block1_1_f1, block1_1_f2, block1_1_f3, block1_1_f4, block1_1_f5,
       block2_1_f1, block2_1_f2, block2_1_f3, block2_1_f4, block2_1_f5, block3_1_o1, block3_1_o2,
       block3_1_o3, block3_1_o4, block3_1_o5, block4_1__05, block4_1_o1, block4_1_o2, block4_1_out_7,
       block4_1_out_8, encoder_1_a, encoder_1_b, encoder_1_c, encoder_1_d, encoder_1_e, not_1_out, not_2_out,
       or_1_out, or_2_out, or_3_out, or_4_out, or_5_out;

  Encoder encoder_1 (
    ._1(a), ._2(b), ._3(c), ._4(d), ._5(e), ._6(f), ._7(g), ._8(h), ._9(i), ._10(j), ._11(k), ._12(l),
    ._13(m), ._14(n), ._15(o), ._16(p), ._17(q), ._18(r), ._19(s), ._20(t), ._21(u), ._22(v), ._23(w),
    ._24(x), ._25(y), ._26(z), .E(encoder_1_e), .D(encoder_1_d), .C(encoder_1_c), .B(encoder_1_b),
    .A(encoder_1_a));
  block1 block1_1 (
    .in_1(encoder_1_a), .in_2(encoder_1_b), .in_3(encoder_1_c), .in_4(encoder_1_d), .E(encoder_1_e),
    .F1(block1_1_f1), .F2(block1_1_f2), .F3(block1_1_f3), .F4(block1_1_f4), .F5(block1_1_f5));
  block2 block2_1 (
    .in_1(encoder_1_a), .B(encoder_1_b), .C(encoder_1_c), .D(encoder_1_d), .E(encoder_1_e), .F1(block2_1_f1),
    .F2(block2_1_f2), .F3(block2_1_f3), .F4(block2_1_f4), .F5(block2_1_f5));
  block3 block3_1 (
    .O2(block3_1_o2), .O1(block3_1_o1), .A(encoder_1_a), .B(encoder_1_b), .C(encoder_1_c), .D(encoder_1_d),
    .E(encoder_1_e), .O5(block3_1_o5), .O4(block3_1_o4), .O3(block3_1_o3));
  block4 block4_1 (
    .in_1(encoder_1_a), .in_2(encoder_1_b), .in_3(encoder_1_c), .D(encoder_1_d), .in_5(encoder_1_e),
    ._05(block4_1__05), .out_7(block4_1_out_7), .out_8(block4_1_out_8), .O2(block4_1_o2), .O1(block4_1_o1));
  not not_1 (not_1_out, in_1);
  not not_2 (not_2_out, in_2);
  and and_1 (and_1_out, block1_1_f1, not_1_out, not_2_out);
  and and_2 (and_2_out, block2_1_f1, not_1_out, in_2);
  and and_3 (and_3_out, block3_1_o5, in_1, not_2_out);
  and and_4 (and_4_out, block4_1__05, in_1, in_2);
  and and_5 (and_5_out, block1_1_f2, not_1_out, not_2_out);
  and and_6 (and_6_out, block2_1_f2, not_1_out, in_2);
  and and_7 (and_7_out, block3_1_o4, in_1, not_2_out);
  and and_8 (and_8_out, block4_1_out_7, in_1, in_2);
  and and_9 (and_9_out, block1_1_f3, not_1_out, not_2_out);
  and and_10 (and_10_out, block2_1_f3, not_1_out, in_2);
  and and_11 (and_11_out, block3_1_o3, in_1, not_2_out);
  and and_12 (and_12_out, block4_1_out_8, in_1, in_2);
  and and_13 (and_13_out, block1_1_f4, not_1_out, not_2_out);
  and and_14 (and_14_out, block2_1_f4, not_1_out, in_2);
  and and_15 (and_15_out, block3_1_o2, in_1, not_2_out);
  and and_16 (and_16_out, block4_1_o2, in_1, in_2);
  and and_17 (and_17_out, block1_1_f5, not_1_out, not_2_out);
  and and_18 (and_18_out, block2_1_f5, not_1_out, in_2);
  and and_19 (and_19_out, block3_1_o1, in_1, not_2_out);
  and and_20 (and_20_out, block4_1_o1, in_1, in_2);
  or or_1 (or_1_out, and_1_out, and_2_out, and_3_out, and_4_out);
  or or_2 (or_2_out, and_5_out, and_6_out, and_7_out, and_8_out);
  or or_3 (or_3_out, and_9_out, and_10_out, and_11_out, and_12_out);
  or or_4 (or_4_out, and_13_out, and_14_out, and_15_out, and_16_out);
  or or_5 (or_5_out, and_17_out, and_18_out, and_19_out, and_20_out);
  Decoder decoder_1 (
    .in_1(or_1_out), .in_2(or_2_out), .in_3(or_3_out), .in_4(or_4_out), .in_5(or_5_out), .z(z_2), .y(y_2),
    .x(x_2), .w(w_2), .v(v_2), .u(u_2), .t(t_2), .s(s_2), .r(r_2), .q(q_2), .p(p_2), .o(o_2), .n(n_2),
    .m(m_2), .l(l_2), .k(k_2), .j(j_2), .i(i_2), .h(h_2), .g(g_2), .f(f_2), .e(e_2), .d(d_2), .c(c_2),
    .b(b_2), .a(a_2));

  // Notes on the sheet:
  //   INPUT
  //   ENCODER
  //   LSB
  //   MSB
  //   Enigma Machine
  //   19BCE259 | 19BCE270 | 19BCE273
  //   BLACK BOXES
  //   LSB
  //   MSB
  //   MSB
  //   LSB
  //   MSB
  //   LSB
  //   MSB
  //   LSB
  //   SETTINGS
  //   DECODER
  //   OUTPUT
endmodule

module block1 (
  input  in_1,
  input  in_2,
  input  in_3,
  input  in_4,
  input  E,
  output F1,
  output F2,
  output F3,
  output F4,
  output F5
);

  wire and_1_out, and_2_out, and_3_out, and_4_out, and_5_out, and_6_out, and_7_out, and_8_out, and_9_out,
       and_10_out, and_11_out, and_12_out, and_13_out, and_14_out, and_15_out, and_16_out, and_17_out,
       and_18_out, and_19_out, and_20_out, and_21_out, and_22_out, and_23_out, and_24_out, and_25_out,
       and_26_out, and_27_out, not_1_out, not_2_out, not_3_out, not_4_out, not_5_out;

  not not_1 (not_1_out, in_1);
  not not_2 (not_2_out, in_2);
  not not_3 (not_3_out, in_3);
  not not_4 (not_4_out, in_4);
  not not_5 (not_5_out, E);
  and and_1 (and_1_out, not_5_out, not_4_out, in_3, not_1_out);
  and and_2 (and_2_out, E, not_3_out, not_2_out, not_1_out);
  and and_3 (and_3_out, E, in_4, not_1_out);
  and and_4 (and_4_out, in_4, not_3_out, not_1_out);
  and and_5 (and_5_out, in_4, not_2_out, not_1_out);
  and and_6 (and_6_out, E, not_4_out, in_3);
  and and_7 (and_7_out, not_5_out, not_4_out, not_3_out);
  and and_8 (and_8_out, not_3_out, in_1, not_2_out);
  and and_9 (and_9_out, not_4_out, not_3_out, not_1_out);
  and and_10 (and_10_out, not_4_out, in_3, in_1);
  and and_11 (and_11_out, not_5_out, in_3, not_2_out);
  and and_12 (and_12_out, not_5_out, not_2_out, not_4_out);
  and and_13 (and_13_out, in_4, in_3, in_1);
  and and_14 (and_14_out, not_5_out, not_4_out, in_1);
  and and_15 (and_15_out, not_5_out, in_3, not_4_out);
  and and_16 (and_16_out, E, in_4, not_3_out, in_2);
  and and_17 (and_17_out, not_4_out, not_3_out, not_2_out, in_1);
  and and_18 (and_18_out, not_5_out, not_3_out, not_2_out, not_1_out);
  and and_19 (and_19_out, not_5_out, not_4_out, not_2_out, in_1);
  and and_20 (and_20_out, not_5_out, not_3_out, not_1_out, in_2);
  and and_21 (and_21_out, E, in_4, not_2_out, not_1_out);
  and and_22 (and_22_out, E, not_3_out, not_2_out, not_1_out);
  and and_23 (and_23_out, in_2, in_1);
  and and_24 (and_24_out, not_5_out, in_1);
  and and_25 (and_25_out, E, not_4_out, not_2_out, not_1_out);
  and and_26 (and_26_out, not_4_out, not_3_out, in_2, not_1_out);
  and and_27 (and_27_out, not_5_out, in_4, not_3_out, not_1_out);
  or or_1 (F1, and_1_out, and_2_out, and_3_out, and_4_out, and_5_out);
  or or_2 (F2, and_16_out, and_17_out, and_18_out, and_6_out, and_7_out);
  or or_3 (F3, and_19_out, and_20_out, and_21_out, and_8_out, and_9_out);
  or or_4 (F4, and_22_out, and_10_out, and_11_out, and_12_out, and_23_out, and_24_out);
  or or_5 (F5, and_25_out, and_26_out, and_27_out, and_13_out, and_14_out, and_15_out);

  // Notes on the sheet:
  //   A
  //   MSB
  //   A
  //   B
  //   B
  //   A
  //   A
  //   A
  //   C
  //   C
  //   B
  //   C
  //   B
  //   C
  //   B
  //   D
  //   D
  //   D
  //   D
  //   C
  //   BLACK BOX 1
  //   E
  //   E
  //   E
  //   E
  //   D
  //   LSB
  //   (Mapping every alphabet to another alphabet)
  //   MSB
  //   LSB
endmodule

module block3 (
  input  A,
  input  B,
  input  C,
  input  D,
  input  E,
  output O5,
  output O4,
  output O3,
  output O2,
  output O1
);

  wire and_1_out, and_2_out, and_3_out, and_4_out, and_5_out, and_6_out, and_7_out, and_8_out, and_9_out,
       and_10_out, and_11_out, and_12_out, and_13_out, and_14_out, and_15_out, and_16_out, and_17_out,
       and_18_out, and_19_out, and_20_out, and_21_out, and_22_out, and_23_out, and_24_out, and_25_out,
       and_26_out, and_27_out, and_28_out, not_1_out, not_2_out, not_3_out, not_4_out, not_5_out;

  not not_1 (not_1_out, A);
  not not_2 (not_2_out, B);
  not not_3 (not_3_out, C);
  not not_4 (not_4_out, D);
  not not_5 (not_5_out, E);
  and and_1 (and_1_out, E, D, C, A);
  and and_2 (and_2_out, not_5_out, D, not_3_out, A);
  and and_3 (and_3_out, not_5_out, not_3_out, B, not_1_out);
  and and_4 (and_4_out, E, not_4_out, not_2_out, not_1_out);
  and and_5 (and_5_out, not_4_out, not_3_out, not_2_out, not_1_out);
  and and_6 (and_6_out, E, C, B);
  and and_7 (and_7_out, not_4_out, C, B);
  and and_8 (and_8_out, E, D, not_3_out, not_2_out, not_1_out);
  and and_9 (and_9_out, not_5_out, not_4_out, A);
  and and_10 (and_10_out, not_5_out, not_4_out, B);
  and and_11 (and_11_out, not_5_out, C, not_2_out);
  and and_12 (and_12_out, B, A);
  and and_13 (and_13_out, E, not_4_out, not_3_out, not_1_out);
  and and_14 (and_14_out, D, not_3_out, A);
  and and_15 (and_15_out, not_5_out, C, A);
  and and_16 (and_16_out, D, C, B);
  and and_17 (and_17_out, E, not_4_out, B);
  and and_18 (and_18_out, not_5_out, D, not_2_out);
  and and_19 (and_19_out, not_5_out, not_3_out, not_2_out, A);
  and and_20 (and_20_out, E, C, not_2_out, not_1_out);
  and and_21 (and_21_out, E, D, not_1_out);
  and and_22 (and_22_out, D, not_2_out, not_1_out);
  and and_23 (and_23_out, D, C);
  and and_24 (and_24_out, not_5_out, D, A);
  and and_25 (and_25_out, not_5_out, not_4_out, C);
  and and_26 (and_26_out, E, D, not_3_out);
  and and_27 (and_27_out, not_4_out, C, not_2_out);
  and and_28 (and_28_out, not_3_out, not_2_out, not_1_out);
  or or_1 (O5, and_1_out, and_2_out, and_3_out, and_4_out, and_5_out, and_6_out, and_7_out);
  or or_2 (O4, and_8_out, and_9_out, and_10_out, and_11_out, and_12_out);
  or or_3 (O3, and_13_out, and_14_out, and_15_out, and_16_out, and_17_out, and_18_out);
  or or_4 (O1, and_24_out, and_25_out, and_26_out, and_27_out, and_28_out);
  or or_5 (O2, and_19_out, and_20_out, and_21_out, and_22_out, and_23_out);

  // Notes on the sheet:
  //   MSB
  //   BLACK BOX 3
  //   LSB
  //   (Mapping every alphabet to another alphabet)
  //   LSB
  //   MSB
endmodule

module block4 (
  input  in_1,
  input  in_2,
  input  in_3,
  input  D,
  input  in_5,
  output _05,
  output out_7,
  output out_8,
  output O2,
  output O1
);

  wire and_1_out, and_2_out, and_3_out, and_4_out, and_5_out, and_6_out, and_7_out, and_8_out, and_9_out,
       and_10_out, and_11_out, and_12_out, and_13_out, and_14_out, and_15_out, and_16_out, and_17_out,
       and_18_out, and_19_out, and_20_out, and_21_out, and_22_out, and_23_out, and_24_out, and_25_out,
       and_26_out, and_27_out, and_28_out, and_29_out, and_30_out, and_31_out, and_32_out, not_1_out,
       not_2_out, not_3_out, not_4_out, not_5_out;

  not not_1 (not_1_out, in_1);
  not not_2 (not_2_out, in_2);
  not not_3 (not_3_out, in_3);
  not not_4 (not_4_out, D);
  not not_5 (not_5_out, in_5);
  and and_1 (and_1_out, not_5_out, D, in_3, in_1);
  and and_2 (and_2_out, not_5_out, not_3_out, in_2, not_1_out);
  and and_3 (and_3_out, in_5, not_3_out, not_2_out, not_1_out);
  and and_4 (and_4_out, in_5, in_2, in_1);
  and and_5 (and_5_out, in_5, D, not_1_out);
  and and_6 (and_6_out, D, in_2);
  and and_7 (and_7_out, in_5, not_4_out, not_3_out, not_2_out, not_1_out);
  and and_8 (and_8_out, not_5_out, not_4_out, not_2_out, in_1);
  and and_9 (and_9_out, not_5_out, D, not_2_out, not_1_out);
  and and_10 (and_10_out, in_5, D, in_1);
  and and_11 (and_11_out, not_5_out, in_3, not_2_out);
  and and_12 (and_12_out, in_3, in_1);
  and and_13 (and_13_out, in_5, D, in_3, in_1);
  and and_14 (and_14_out, not_5_out, not_4_out, in_3, in_1);
  and and_15 (and_15_out, in_5, not_4_out, not_3_out, in_1);
  and and_16 (and_16_out, not_5_out, D, not_2_out, not_1_out);
  and and_17 (and_17_out, not_5_out, not_4_out, not_3_out, not_1_out);
  and and_18 (and_18_out, D, in_3, in_2);
  and and_19 (and_19_out, in_5, not_4_out, in_2);
  and and_20 (and_20_out, not_5_out, not_4_out, not_2_out, in_1);
  and and_21 (and_21_out, in_5, D, not_3_out, not_2_out);
  and and_22 (and_22_out, in_5, D, in_1);
  and and_23 (and_23_out, in_5, not_3_out, in_1);
  and and_24 (and_24_out, not_4_out, in_3, in_2);
  and and_25 (and_25_out, not_5_out, D, in_2);
  and and_26 (and_26_out, not_3_out, not_2_out, in_1);
  and and_27 (and_27_out, not_4_out, not_3_out, not_2_out, in_1);
  and and_28 (and_28_out, D, in_3, not_2_out, not_1_out);
  and and_29 (and_29_out, not_5_out, not_3_out, in_2);
  and and_30 (and_30_out, not_5_out, D, in_3);
  and and_31 (and_31_out, not_5_out, not_4_out, not_2_out);
  and and_32 (and_32_out, not_5_out, in_1);
  or or_1 (_05, and_1_out, and_2_out, and_3_out, and_4_out, and_5_out, and_6_out);
  or or_2 (out_7, and_7_out, and_8_out, and_9_out, and_10_out, and_11_out, and_12_out);
  or or_3 (out_8, and_13_out, and_14_out, and_15_out, and_16_out, and_17_out, and_18_out, and_19_out);
  or or_4 (O1, and_27_out, and_28_out, and_29_out, and_30_out, and_31_out, and_32_out);
  or or_5 (O2, and_20_out, and_21_out, and_22_out, and_23_out, and_24_out, and_25_out, and_26_out);

  // Notes on the sheet:
  //   MSB
  //   A
  //   B
  //   C
  //   BLACK BOX 4
  //   E
  //   LSB
  //   (Mapping every alphabet to another alphabet)
  //   MSB
  //   LSB
  //   O4
  //   O3
endmodule

module Decoder (
  input  in_1,
  input  in_2,
  input  in_3,
  input  in_4,
  input  in_5,
  output z,
  output y,
  output x,
  output w,
  output v,
  output u,
  output t,
  output s,
  output r,
  output q,
  output p,
  output o,
  output n,
  output m,
  output l,
  output k,
  output j,
  output i,
  output h,
  output g,
  output f,
  output e,
  output d,
  output c,
  output b,
  output a
);

  wire not_1_out, not_2_out, not_3_out, not_4_out, not_5_out;

  not not_1 (not_1_out, in_1);
  not not_2 (not_2_out, in_2);
  not not_3 (not_3_out, in_3);
  not not_4 (not_4_out, in_4);
  not not_5 (not_5_out, in_5);
  and and_1 (z, in_5, not_4_out, not_3_out, in_2, in_1);
  and and_2 (y, not_5_out, not_4_out, not_3_out, in_2, in_1);
  and and_3 (x, in_5, in_4, in_3, not_2_out, in_1);
  and and_4 (w, not_5_out, in_4, in_3, not_2_out, in_1);
  and and_5 (v, in_5, not_4_out, in_3, not_2_out, in_1);
  and and_6 (u, not_5_out, not_4_out, in_3, not_2_out, in_1);
  and and_7 (t, in_5, in_4, not_3_out, not_2_out, in_1);
  and and_8 (s, not_5_out, in_4, not_3_out, not_2_out, in_1);
  and and_9 (r, in_5, not_4_out, not_3_out, not_2_out, in_1);
  and and_10 (q, not_5_out, not_4_out, not_3_out, not_2_out, in_1);
  and and_11 (p, in_5, in_4, in_3, in_2, not_1_out);
  and and_12 (o, not_5_out, in_4, in_3, in_2, not_1_out);
  and and_13 (n, in_5, not_4_out, in_3, in_2, not_1_out);
  and and_14 (m, not_5_out, not_4_out, in_3, in_2, not_1_out);
  and and_15 (l, in_5, in_4, not_3_out, in_2, not_1_out);
  and and_16 (k, not_5_out, in_4, not_3_out, in_2, not_1_out);
  and and_17 (j, in_5, not_4_out, not_3_out, in_2, not_1_out);
  and and_18 (i, not_5_out, not_4_out, not_3_out, in_2, not_1_out);
  and and_19 (h, in_5, in_4, in_3, not_2_out, not_1_out);
  and and_20 (g, not_5_out, in_4, in_3, not_2_out, not_1_out);
  and and_21 (f, in_5, not_4_out, in_3, not_2_out, not_1_out);
  and and_22 (e, not_5_out, not_4_out, in_3, not_2_out, not_1_out);
  and and_23 (d, in_5, in_4, not_3_out, not_2_out, not_1_out);
  and and_24 (c, not_5_out, in_4, not_3_out, not_2_out, not_1_out);
  and and_25 (b, in_5, not_4_out, not_3_out, not_2_out, not_1_out);
  and and_26 (a, not_5_out, not_4_out, not_3_out, not_2_out, not_1_out);

  // Notes on the sheet:
  //   MSB
  //   DECODER
  //   LSB
  //   (Binary to Alphabet encoding)
endmodule

module block2 (
  input  in_1,
  input  B,
  input  C,
  input  D,
  input  E,
  output F1,
  output F2,
  output F3,
  output F4,
  output F5
);

  wire and_1_out, and_2_out, and_3_out, and_4_out, and_5_out, and_6_out, and_7_out, and_8_out, and_9_out,
       and_10_out, and_11_out, and_12_out, and_13_out, and_14_out, and_15_out, and_16_out, and_17_out,
       and_18_out, and_19_out, and_20_out, and_21_out, and_22_out, and_23_out, and_24_out, and_25_out,
       and_26_out, and_27_out, and_28_out, not_1_out, not_2_out, not_3_out, not_4_out, not_5_out;

  not not_1 (not_1_out, in_1);
  not not_2 (not_2_out, B);
  not not_3 (not_3_out, C);
  not not_4 (not_4_out, E);
  not not_5 (not_5_out, D);
  and and_1 (and_1_out, E, not_3_out, B);
  and and_2 (and_2_out, not_4_out, not_5_out, C);
  and and_3 (and_3_out, not_3_out, B, not_1_out);
  and and_4 (and_4_out, not_5_out, not_3_out, not_1_out);
  and and_5 (and_5_out, E, not_3_out, not_2_out, in_1);
  and and_6 (and_6_out, not_4_out, not_5_out, not_3_out, B);
  and and_7 (and_7_out, not_4_out, D, C, not_2_out);
  and and_8 (and_8_out, not_4_out, not_5_out, in_1);
  and and_9 (and_9_out, E, C, B);
  and and_10 (and_10_out, not_1_out, C, D);
  and and_11 (and_11_out, not_4_out, D, not_3_out, in_1);
  and and_12 (and_12_out, E, not_5_out, in_1, not_3_out);
  and and_13 (and_13_out, not_5_out, not_3_out, not_2_out, not_1_out);
  and and_14 (and_14_out, D, not_4_out, B);
  and and_15 (and_15_out, E, C, not_1_out);
  and and_16 (and_16_out, not_1_out, B, not_5_out, E);
  and and_17 (and_17_out, not_1_out, not_2_out, not_3_out, D);
  and and_18 (and_18_out, not_4_out, C, D);
  and and_19 (and_19_out, not_4_out, D, not_1_out);
  and and_20 (and_20_out, E, D, not_3_out, in_1);
  and and_21 (and_21_out, not_4_out, not_3_out, not_2_out, not_1_out);
  and and_22 (and_22_out, not_5_out, C, B);
  and and_23 (and_23_out, E, C, not_1_out);
  and and_24 (and_24_out, E, not_1_out, not_5_out);
  and and_25 (and_25_out, not_5_out, C, in_1);
  and and_26 (and_26_out, not_1_out, not_2_out, C, not_5_out);
  and and_27 (and_27_out, not_2_out, not_3_out, not_4_out, not_5_out);
  and and_28 (and_28_out, not_4_out, not_5_out, not_3_out, not_2_out);
  or or_1 (F2, and_5_out, and_6_out, and_7_out, and_8_out, and_9_out);
  or or_2 (F3, and_10_out, and_11_out, and_12_out, and_13_out, and_14_out, and_15_out);
  or or_3 (F4, and_16_out, and_26_out, and_17_out, and_27_out, and_18_out, and_19_out);
  or or_4 (F1, and_1_out, and_2_out, and_3_out, and_4_out);
  or or_5 (F5, and_20_out, and_28_out, and_21_out, and_22_out, and_23_out, and_24_out, and_25_out);

  // Notes on the sheet:
  //   A
  //   A
  //   A
  //   A
  //   MSB
  //   B
  //   B
  //   B
  //   B
  //   A
  //   C
  //   C
  //   C
  //   C
  //   BLACK BOX 2
  //   D
  //   D
  //   D
  //   D
  //   E
  //   E
  //   E
  //   E
  //   LSB
  //   (Mapping every alphabet to another alphabet)
  //   MSB
  //   LSB
endmodule

module Encoder (
  input  _1,
  input  _2,
  input  _3,
  input  _4,
  input  _5,
  input  _6,
  input  _7,
  input  _8,
  input  _9,
  input  _10,
  input  _11,
  input  _12,
  input  _13,
  input  _14,
  input  _15,
  input  _16,
  input  _17,
  input  _18,
  input  _19,
  input  _20,
  input  _21,
  input  _22,
  input  _23,
  input  _24,
  input  _25,
  input  _26,
  output E,
  output D,
  output C,
  output B,
  output A
);

  or or_1 (E, _2, _4, _6, _8, _10, _12, _14, _16, _18, _20, _22, _24, _26);
  or or_2 (D, _3, _4, _7, _8, _11, _12, _15, _16, _19, _20, _23, _24);
  or or_3 (C, _5, _6, _7, _8, _13, _14, _15, _16, _21, _22, _23, _24);
  or or_4 (B, _9, _10, _11, _12, _13, _14, _15, _16, _25, _26);
  or or_5 (A, _17, _18, _19, _20, _21, _22, _23, _24, _25, _26);

  // Notes on the sheet:
  //   1
  //   1
  //   2
  //   3
  //   2
  //   3
  //   4
  //   5
  //   5
  //   4
  //   7
  //   6
  //   6
  //   7
  //   8
  //   9
  //   8
  //   9
  //   ENCODER
  //   10
  //   11
  //   10
  //   11
  //   12
  //   13
  //   12
  //   13
  //   ( Alphabet to binary encoding)
  //   14
  //   15
  //   15
  //   14
  //   17
  //   16
  //   17
  //   16
  //   19
  //   18
  //   19
  //   18
  //   20
  //   21
  //   20
  //   21
  //   23
  //   22
  //   22
  //   23
  //   24
  //   25
  //   24
  //   25
  //   26
  //   26
endmodule
